// Logisim project G2.circ as structural Verilog: 9 circuits, main circuit main
module main (
  input  in_1,
  output out_2,
  output out_3,
  output WB_rt,
  output WB_rd,
  output EX_rt,
  output EX_rs,
  output MEM_rt,
  output MEM_rs,
  output out_10,
  output out_11
);

  wire ALUjump, ALUSrc, Branch, clock_1_out, clock_2_out, clock_3_out, clock_4_out, clock_5_out, clock_6_out,
       clock_7_out, clock_8_out, jal, Jump, MemRead, MemtoReg, MemWrite, nand_1_out, nor_1_out, not_1_out,
       not_2_out, not_3_out, not_4_out, or_1_out, RegDst, RegWrite, state_1_memtoreg, state_1_memtoreg_2,
       state_1_memtoreg_out, state_1_memtoreg_out_2, state_1_memtoreg_out_3, state_1_memtoreg_out_4,
       state_1_memtoreg_out_5, state_1_memtoreg_out_6, state_2_memtoreg, state_2_memtoreg_2,
       state_2_memtoreg_out, state_2_memtoreg_out_2, state_3_memtoreg_out, WriteEnable;
  wire [1:0] check_type_1_type;
  wire [2:0] ALUOp, state_1_regwrite_out_2;
  wire [3:0] ALUOp_alu, if_id_1_pc_out_2;
  wire [4:0] multiplexer_2_out, multiplexer_4_out, rd_EX, rd_MEM, rd_WB;
  wire [5:0] Control, id_ex_1_aluop_out, if_id_1_instruction_out;
  wire [25:6] if_id_1_instruction_out_2;
  wire [27:0] bit_extender_1_out, if_id_1_pc_out, shifter_1_out;
  wire [31:0] adder_1_p3, bit_extender_2_out, ex_mem_1_alu_result_out, ex_mem_1_read_data_2_2, EXResult,
       id_ex_1_pc_out, id_ex_1_read_data_1_out, id_ex_1_read_data_2_out, id_ex_1_sign_ext_out,
       mem_wb_1_alu_result_out, mem_wb_1_memout_out, mips_ram_1_p7, mipsprogramrom_1_p2, multiplexer_1_out,
       multiplexer_3_out, multiplexer_5_out, multiplexer_6_out, multiplexer_7_out, multiplexer_8_out,
       multiplexer_9_out, multiplexer_10_out, PC_q, registerfile_1_p9, registerfile_1_p10, shifter_2_out,
       WriteData;

  Clock clock_1 (.out(clock_1_out));
  Register #(.width(32)) PC (.D(multiplexer_1_out), .Q(PC_q), .clk(clock_1_out), .clr(in_1));  // open: en
  Multiplexer #(.width(32), .enable("false")) multiplexer_1 (
    .in0(multiplexer_10_out), .in1(adder_1_p3), .out(multiplexer_1_out), .sel(nor_1_out));
  // Adder adder_1: pin names not known; wires that end beside it: PC_q, 32'h4, adder_1_p3
  // MIPSProgramROM mipsprogramrom_1: pin names not known; wires that end beside it: PC_q, mipsprogramrom_1_p2
  IF_ID if_id_1 (
    .Clock(clock_2_out), .PC_in(adder_1_p3), .Instruction_in(mipsprogramrom_1_p2),
    .PC_out({if_id_1_pc_out_2, if_id_1_pc_out}),
    .Instruction_out({Control, if_id_1_instruction_out_2, if_id_1_instruction_out}), .Clear(out_2));
  Clock clock_2 (.out(clock_2_out));
  Check_type check_type_1 (.OP(Control), .\type (check_type_1_type));
  Data_Hazard data_hazard_1 (
    .rd(if_id_1_instruction_out_2[25:21]), .rd_2(rd_WB), .rt(if_id_1_instruction_out_2[20:16]),
    .\type (check_type_1_type), .Alert_rt(WB_rd), .Alert_rs(WB_rt));
  Data_Hazard data_hazard_2 (
    .rd(if_id_1_instruction_out_2[25:21]), .rd_2(rd_EX), .rt(if_id_1_instruction_out_2[20:16]),
    .\type (check_type_1_type), .Alert_rt(EX_rs), .Alert_rs(EX_rt));
  Data_Hazard data_hazard_3 (
    .rd(if_id_1_instruction_out_2[25:21]), .rd_2(rd_MEM), .rt(if_id_1_instruction_out_2[20:16]),
    .\type (check_type_1_type), .Alert_rt(MEM_rs), .Alert_rs(MEM_rt));
  Multiplexer #(.width(5), .enable("false")) multiplexer_2 (
    .in0(if_id_1_instruction_out_2[20:16]), .in1(if_id_1_instruction_out_2[15:11]), .out(multiplexer_2_out),
    .sel(RegDst));
  // PLA Control: pin names not known; wires that end beside it: Control
  not not_1 (not_1_out, state_1_memtoreg_out_4);
  Multiplexer #(.width(32), .enable("false")) multiplexer_3 (
    .in0({if_id_1_pc_out_2, if_id_1_pc_out}), .in1(WriteData), .out(multiplexer_3_out), .sel(not_1_out));
  Multiplexer #(.width(5), .enable("false")) multiplexer_4 (
    .in0({5{1'b1}}), .in1(multiplexer_2_out), .out(multiplexer_4_out), .sel(not_1_out));
  assign bit_extender_1_out = {{2{1'b0}}, {if_id_1_instruction_out_2, if_id_1_instruction_out}};  // Bit_Extender bit_extender_1
  Clock clock_3 (.out(clock_3_out));
  Shifter #(.width(28)) shifter_1 (.in(bit_extender_1_out), .\dist (5'b00010), .out(shifter_1_out));
  assign bit_extender_2_out = {{16{1'b0}}, {if_id_1_instruction_out_2[15:6], if_id_1_instruction_out}};  // Bit_Extender bit_extender_2
  // RegisterFile registerfile_1: pin names not known; wires that end beside it: bit_extender_1_out, multiplexer_3_out, clock_3_out, WriteEnable, rd_WB, if_id_1_instruction_out_2[25:21], if_id_1_instruction_out_2[20:16], in_1, registerfile_1_p9, registerfile_1_p10
  Clock clock_4 (.out(clock_4_out));
  not not_2 (not_2_out, nor_1_out);
  Multiplexer #(.width(32), .enable("false")) multiplexer_5 (
    .in0(EXResult), .in1(registerfile_1_p9), .out(multiplexer_5_out), .sel(EX_rs));
  Multiplexer #(.width(32), .enable("false")) multiplexer_6 (
    .in0(EXResult), .in1(registerfile_1_p10), .out(multiplexer_6_out), .sel(EX_rt));
  D_Flip_Flop #(.trigger("falling")) d_ff_1 (
    .clk(clock_4_out), .D(not_2_out), .Q(out_2), .Qn(out_3), .en(1'b1), .reset(1'b0));  // open: preset
  nor nor_1 (nor_1_out, state_1_memtoreg_out_5, state_1_memtoreg_out_6, ALUjump, state_1_memtoreg_out_4);
  ID_EX id_ex_1 (
    .Clock(clock_5_out), .PC_in({if_id_1_pc_out_2, if_id_1_pc_out}), .Read_Data_1_in(multiplexer_5_out),
    .Read_Data_2_in(multiplexer_6_out), .Sign_Ext_in(bit_extender_2_out), .PC_out(id_ex_1_pc_out),
    .Read_Data_1_out(id_ex_1_read_data_1_out), .Read_Data_2_out(id_ex_1_read_data_2_out),
    .Sign_Ext_out(id_ex_1_sign_ext_out), .ALUOp_in(if_id_1_instruction_out), .ALUOp_out(id_ex_1_aluop_out),
    .Clear(out_2));
  Clock clock_5 (.out(clock_5_out));
  State state_1 (
    .Clock(clock_5_out), .RegWrite_in(multiplexer_4_out), .MemToReg_in(RegWrite), .MemToReg_in_2(MemtoReg),
    .RegWrite_out(rd_EX), .MemToReg(state_1_memtoreg), .MemToReg_out(state_1_memtoreg_out),
    .MemToReg_in_3(MemRead), .MemToReg_2(state_1_memtoreg_2), .MemToReg_in_4(MemWrite),
    .MemToReg_out_2(state_1_memtoreg_out_2), .MemToReg_in_5(ALUSrc), .MemToReg_out_3(state_1_memtoreg_out_3),
    .RegWrite_in_2(ALUOp), .RegWrite_out_2(state_1_regwrite_out_2), .MemToReg_in_6(Jump),
    .MemToReg_out_4(state_1_memtoreg_out_4), .MemToReg_in_7(Branch), .MemToReg_out_5(state_1_memtoreg_out_5),
    .MemToReg_in_8(jal), .MemToReg_out_6(state_1_memtoreg_out_6));  // open: RegWrite_in_3, RegWrite_out_3, RegWrite_in_4, RegWrite_out_4
  Multiplexer #(.width(32), .enable("false")) multiplexer_7 (
    .in0(id_ex_1_pc_out), .in1(id_ex_1_read_data_1_out), .out(multiplexer_7_out), .sel(or_1_out));
  or or_1 (or_1_out, state_1_memtoreg_out_4, ALUjump);
  Multiplexer #(.width(32), .enable("false")) multiplexer_8 (
    .in0(id_ex_1_read_data_2_out), .in1(id_ex_1_sign_ext_out), .out(multiplexer_8_out),
    .sel(state_1_memtoreg_out_3));
  ALUOp u_ALUOp (.ALUOp(state_1_regwrite_out_2), .funct(id_ex_1_aluop_out), .ALU(ALUOp_alu), .JUMP(ALUjump));
  Multiplexer #(.width(32), .enable("false")) multiplexer_9 (
    .in0({if_id_1_pc_out_2, shifter_1_out}), .in1(multiplexer_7_out), .out(multiplexer_9_out), .sel(not_3_out));
  not not_3 (not_3_out, state_1_memtoreg_out_6);
  Shifter #(.width(32)) shifter_2 (.in(id_ex_1_sign_ext_out), .\dist (5'b00010), .out(shifter_2_out));
  // MIPS_ALU mips_alu_1: pin names not known; wires that end beside it: id_ex_1_read_data_2_out, id_ex_1_read_data_1_out, multiplexer_8_out, ALUOp_alu, out_10, EXResult, out_11
  Multiplexer #(.width(32), .enable("false")) multiplexer_10 (
    .in0(shifter_2_out), .in1(multiplexer_9_out), .out(multiplexer_10_out), .sel(nand_1_out));
  nand nand_1 (nand_1_out, out_10, state_1_memtoreg_out_5);
  EX_MEM ex_mem_1 (
    .Clock(clock_6_out), .PC_in(multiplexer_10_out), .ALU_result_in(EXResult),
    .Read_Data_2(id_ex_1_read_data_2_out), .ALU_result_out(ex_mem_1_alu_result_out),
    .Read_Data_2_2(ex_mem_1_read_data_2_2));  // open: PC_out
  Clock clock_6 (.out(clock_6_out));
  State state_2 (
    .Clock(clock_6_out), .RegWrite_in(rd_EX), .MemToReg_in(state_1_memtoreg),
    .MemToReg_in_2(state_1_memtoreg_out), .RegWrite_out(rd_MEM), .MemToReg(state_2_memtoreg),
    .MemToReg_out(state_2_memtoreg_out), .MemToReg_in_3(state_1_memtoreg_2), .MemToReg_2(state_2_memtoreg_2),
    .MemToReg_in_4(state_1_memtoreg_out_2), .MemToReg_out_2(state_2_memtoreg_out_2));  // open: MemToReg_in_5, MemToReg_out_3, RegWrite_in_2, RegWrite_out_2, MemToReg_in_6, MemToReg_out_4, MemToReg_in_7, MemToReg_out_5, MemToReg_in_8, MemToReg_out_6, RegWrite_in_3, RegWrite_out_3, RegWrite_in_4, RegWrite_out_4
  not not_4 (not_4_out, clock_7_out);
  Clock clock_7 (.out(clock_7_out));
  // MIPS_RAM mips_ram_1: pin names not known; wires that end beside it: ex_mem_1_alu_result_out[23:0], ex_mem_1_read_data_2_2, state_2_memtoreg_2, state_2_memtoreg_out_2, not_4_out, in_1, mips_ram_1_p7
  MEM_WB mem_wb_1 (
    .Clock(clock_8_out), .MemOut_in(mips_ram_1_p7), .ALU_result_in(ex_mem_1_alu_result_out),
    .MemOut_out(mem_wb_1_memout_out), .ALU_result_out(mem_wb_1_alu_result_out));
  Clock clock_8 (.out(clock_8_out));
  State state_3 (
    .Clock(clock_8_out), .RegWrite_in(rd_MEM), .MemToReg_in(state_2_memtoreg),
    .MemToReg_in_2(state_2_memtoreg_out), .RegWrite_out(rd_WB), .MemToReg(WriteEnable),
    .MemToReg_out(state_3_memtoreg_out));  // open: MemToReg_in_3, MemToReg_2, MemToReg_in_4, MemToReg_out_2, MemToReg_in_5, MemToReg_out_3, RegWrite_in_2, RegWrite_out_2, MemToReg_in_6, MemToReg_out_4, MemToReg_in_7, MemToReg_out_5, MemToReg_in_8, MemToReg_out_6, RegWrite_in_3, RegWrite_out_3, RegWrite_in_4, RegWrite_out_4
  Multiplexer #(.width(32), .enable("false")) multiplexer_11 (
    .in0(mem_wb_1_memout_out), .in1(mem_wb_1_alu_result_out), .out(WriteData), .sel(state_3_memtoreg_out));
  // MIPSProgramROM mipsprogramrom_2: pin names not known

  // Other names for the same wires on the sheet: Clear = in_1; Flush_pipeline = out_2; RegAddress[4:0] = rd_WB

  // Notes on the sheet:
  //   PC
  //   Inst.
  //   IF/ID
  //   rs
  //   rt
  //   Write Dest
  //   Jump og jal skal i state
  //   ID/EX
  //   PC
  //   Immediate
  //   EX/MEM
  //   PC
  //   ALU result
  //   Register B
  //   MEM/WB
endmodule

module ALUOp (
  input  [2:0] ALUOp,
  input  [5:0] funct,
  output [3:0] ALU,
  output JUMP
);

  // PLA pla_1: pin names not known; wires that end beside it: {ALUOp, funct}
endmodule

module IF_ID (
  input  Clock,
  input  Clear,
  input  [31:0] PC_in,
  input  [31:0] Instruction_in,
  output [31:0] PC_out,
  output [31:0] Instruction_out
);

  Register #(.width(32), .trigger("low")) PC (.D(PC_in), .en(1'b1), .Q(PC_out), .clk(Clock), .clr(Clear));
  Register #(.width(32), .trigger("low")) Instruction (
    .D(Instruction_in), .en(1'b1), .Q(Instruction_out), .clk(Clock), .clr(Clear));
endmodule

module ID_EX (
  input  Clock,
  input  Clear,
  input  [31:0] PC_in,
  input  [31:0] Read_Data_1_in,
  input  [31:0] Read_Data_2_in,
  input  [31:0] Sign_Ext_in,
  input  [5:0] ALUOp_in,
  output [31:0] PC_out,
  output [31:0] Read_Data_1_out,
  output [31:0] Read_Data_2_out,
  output [31:0] Sign_Ext_out,
  output [5:0] ALUOp_out
);

  Register #(.width(32), .trigger("falling")) PC (.D(PC_in), .en(1'b1), .Q(PC_out), .clk(Clock), .clr(Clear));
  Register #(.width(32), .trigger("falling")) Read_Data_1 (
    .D(Read_Data_1_in), .en(1'b1), .Q(Read_Data_1_out), .clk(Clock), .clr(Clear));
  Register #(.width(32), .trigger("falling")) Read_Data_2 (
    .D(Read_Data_2_in), .en(1'b1), .Q(Read_Data_2_out), .clk(Clock), .clr(Clear));
  Register #(.width(32), .trigger("falling")) Sign_Ext (
    .D(Sign_Ext_in), .en(1'b1), .Q(Sign_Ext_out), .clk(Clock), .clr(Clear));
  Register #(.width(6), .trigger("falling")) ALUOp (.D(ALUOp_in), .en(1'b1), .Q(ALUOp_out), .clk(Clock), .clr(Clear));
endmodule

module EX_MEM (
  input  Clock,
  input  [31:0] PC_in,
  input  [31:0] ALU_result_in,
  input  [31:0] Read_Data_2,
  output [31:0] PC_out,
  output [31:0] ALU_result_out,
  output [31:0] Read_Data_2_2
);

  Register #(.width(32), .trigger("falling")) PC (.D(PC_in), .en(1'b1), .Q(PC_out), .clk(Clock), .clr(1'b0));
  Register #(.width(32), .trigger("falling")) ALU (
    .D(ALU_result_in), .en(1'b1), .Q(ALU_result_out), .clk(Clock), .clr(1'b0));
  Register #(.width(32), .trigger("falling")) u_Read_Data_2 (
    .D(Read_Data_2), .en(1'b1), .Q(Read_Data_2_2), .clk(Clock), .clr(1'b0));
endmodule

module MEM_WB (
  input  Clock,
  input  [31:0] MemOut_in,
  input  [31:0] ALU_result_in,
  output [31:0] MemOut_out,
  output [31:0] ALU_result_out
);

  Register #(.width(32), .trigger("falling")) MemOut (
    .D(MemOut_in), .en(1'b1), .Q(MemOut_out), .clk(Clock), .clr(1'b0));
  Register #(.width(32), .trigger("falling")) ALU (
    .D(ALU_result_in), .en(1'b1), .Q(ALU_result_out), .clk(Clock), .clr(1'b0));
endmodule

module State (
  input  Clock,
  input  [4:0] RegWrite_in,
  input  MemToReg_in,
  input  MemToReg_in_2,
  input  MemToReg_in_3,
  input  MemToReg_in_4,
  input  MemToReg_in_5,
  input  [2:0] RegWrite_in_2,
  input  MemToReg_in_6,
  input  MemToReg_in_7,
  input  MemToReg_in_8,
  input  [4:0] RegWrite_in_3,
  input  [4:0] RegWrite_in_4,
  output [4:0] RegWrite_out,
  output MemToReg,
  output MemToReg_out,
  output MemToReg_2,
  output MemToReg_out_2,
  output MemToReg_out_3,
  output [2:0] RegWrite_out_2,
  output MemToReg_out_4,
  output MemToReg_out_5,
  output MemToReg_out_6,
  output [4:0] RegWrite_out_3,
  output [4:0] RegWrite_out_4
);

  Register #(.width(5), .trigger("falling")) RegWrite (
    .D(RegWrite_in), .en(1'b1), .Q(RegWrite_out), .clk(Clock), .clr(1'b0));
  Register #(.width(1), .trigger("falling")) u_MemToReg (
    .D(MemToReg_in), .en(1'b1), .Q(MemToReg), .clk(Clock), .clr(1'b0));
  Register #(.width(1), .trigger("falling")) u_MemToReg_2 (
    .D(MemToReg_in_2), .en(1'b1), .Q(MemToReg_out), .clk(Clock), .clr(1'b0));
  Register #(.width(1), .trigger("falling")) MemToReg_3 (
    .D(MemToReg_in_3), .en(1'b1), .Q(MemToReg_2), .clk(Clock), .clr(1'b0));
  Register #(.width(1), .trigger("falling")) MemToReg_4 (
    .D(MemToReg_in_4), .en(1'b1), .Q(MemToReg_out_2), .clk(Clock), .clr(1'b0));
  Register #(.width(1), .trigger("falling")) MemToReg_5 (
    .D(MemToReg_in_5), .en(1'b1), .Q(MemToReg_out_3), .clk(Clock), .clr(1'b0));
  Register #(.width(3), .trigger("falling")) RegWrite_2 (
    .D(RegWrite_in_2), .en(1'b1), .Q(RegWrite_out_2), .clk(Clock), .clr(1'b0));
  Register #(.width(1), .trigger("falling")) MemToReg_6 (
    .D(MemToReg_in_6), .en(1'b1), .Q(MemToReg_out_4), .clk(Clock), .clr(1'b0));
  Register #(.width(1), .trigger("falling")) MemToReg_7 (
    .D(MemToReg_in_7), .en(1'b1), .Q(MemToReg_out_5), .clk(Clock), .clr(1'b0));
  Register #(.width(1), .trigger("falling")) MemToReg_8 (
    .D(MemToReg_in_8), .en(1'b1), .Q(MemToReg_out_6), .clk(Clock), .clr(1'b0));
  Register #(.width(5), .trigger("falling")) RegWrite_3 (
    .D(RegWrite_in_3), .en(1'b1), .Q(RegWrite_out_3), .clk(Clock), .clr(1'b0));
  Register #(.width(5), .trigger("falling")) RegWrite_4 (
    .D(RegWrite_in_4), .en(1'b1), .Q(RegWrite_out_4), .clk(Clock), .clr(1'b0));

  // Notes on the sheet:
  //   Navne passer ikke
endmodule

module Data_Hazard (
  input  [1:0] \type ,
  input  [4:0] rd,
  input  [4:0] rd_2,
  input  [4:0] rt,
  output Alert_rs,
  output Alert_rt
);

  wire mips_alu_1_p4, mips_alu_1_p5, mips_alu_2_p4, mips_alu_3_p4, not_1_out;
  wire [31:0] bit_extender_1_out, bit_extender_2_out, bit_extender_3_out;

  assign bit_extender_1_out = {{27{1'b0}}, rd_2};  // Bit_Extender bit_extender_1
  not not_1 (not_1_out, mips_alu_1_p4);
  // MIPS_ALU mips_alu_1: pin names not known; wires that end beside it: bit_extender_1_out, {32{1'b0}}, 4'b0010, mips_alu_1_p4, mips_alu_1_p5
  assign bit_extender_2_out = {{27{1'b0}}, rd};  // Bit_Extender bit_extender_2
  assign bit_extender_3_out = {{27{1'b0}}, rt};  // Bit_Extender bit_extender_3
  // MIPS_ALU mips_alu_2: pin names not known; wires that end beside it: bit_extender_2_out, mips_alu_1_p5, 4'b0110, mips_alu_2_p4
  // MIPS_ALU mips_alu_3: pin names not known; wires that end beside it: mips_alu_1_p5, bit_extender_3_out, 4'b0110, mips_alu_3_p4, not_1_out
  and and_1 (Alert_rs, \type [0], not_1_out, mips_alu_2_p4);
  and and_2 (Alert_rt, \type [1], \type [0], mips_alu_3_p4);

  // Notes on the sheet:
  //   (add)
  //   (Subu)
  //   (Subu)
endmodule

module Check_type (
  input  [5:0] OP,
  output [1:0] \type 
);

  // PLA pla_1: pin names not known; wires that end beside it: OP, \type 
endmodule
